// Logisim project ALU.circ as structural Verilog: 3 circuits, main circuit ALU
module ALU (
  input  [15:0] B,
  input  [15:0] A,
  input  [3:0] Sel,
  output [15:0] Result
);

  wire n16_bit_adder_1_cout, n16_bit_adder_1_v, or_2_out, W1, W2;
  wire [1:0] not_2_out;
  wire [15:0] ADD_SUB, AND, OR, SLL, SLT, SLTU, SRA, SRL, XOR, xor_1_out;
  wire [15:15] and_2_out;

  assign xor_1_out = B ^ {16{and_2_out[15]}};  // XOR_Gate xor_1, 16 bits wide
  assign XOR = A ^ B;  // XOR_Gate xor_2, 16 bits wide
  assign OR = A | B;  // OR_Gate or_1, 16 bits wide
  _16_Bit_Adder u_16_bit_adder_1 (
    .A(A), .B(xor_1_out), .Cin(and_2_out[15]), .Sum(ADD_SUB), .V(n16_bit_adder_1_v),
    .Cout(n16_bit_adder_1_cout));
  assign SLT = {{15{1'b0}}, W1};  // Bit_Extender bit_extender_1
  assign SLTU = {{15{1'b0}}, W2};  // Bit_Extender bit_extender_2
  xor xor_3 (W1, ADD_SUB[15], n16_bit_adder_1_v);
  not not_1 (W2, n16_bit_adder_1_cout);
  assign AND = A & B;  // AND_Gate and_1, 16 bits wide
  Shifter #(.width(16)) shifter_1 (.in(A), .\dist (B[3:0]), .out(SLL));
  Shifter #(.width(16), .shift("lr")) shifter_2 (.in(A), .\dist (B[3:0]), .out(SRL));
  Multiplexer #(.select(4), .width(16), .enable("false")) multiplexer_1 (
    .in0(ADD_SUB), .in1(ADD_SUB), .in2(SLT), .in3(SLTU), .in4(XOR), .in5(OR), .in6(AND), .in7(SLL),
    .in8(SRL), .in9(SRA), .in10({B[10:0], {5{1'b0}}}), .in11({16{1'b0}}), .in12({16{1'b0}}),
    .in13({16{1'b0}}), .in14({16{1'b0}}), .in15({16{1'b0}}), .out(Result), .sel(Sel));
  Shifter #(.width(16), .shift("ar")) shifter_3 (.in(A), .\dist (B[3:0]), .out(SRA));
  assign not_2_out = ~Sel[3:2];  // NOT_Gate not_2, 2 bits wide
  or or_2 (or_2_out, Sel[1], Sel[0]);
  and and_2 (and_2_out[15], not_2_out[0], not_2_out[1], or_2_out, 1'b1);

  // Other names for the same wires on the sheet: A1[15:0] = A; A2[15:0] = A; B1[15:0] = B; B2[15:0] = B;
  //   LUI[15:5] = B[10:0]

  // Notes on the sheet:
  //   0)ADD
  //   1)SUB
  //   2)SLT
  //   3)SLTU
  //   4)XOR
  //   5)OR
  //   6)AND
  //   7)SLL
  //   8)SRL
  //   9)SRA
  //   10)LUI
endmodule

module FullAdder (
  input  A,
  input  B,
  input  Cin,
  output Sum,
  output Cout
);

  wire and_1_out, and_2_out, xor_1_out;

  xor xor_1 (xor_1_out, A, B);
  and and_1 (and_1_out, Cin, xor_1_out);
  and and_2 (and_2_out, A, B);
  xor xor_2 (Sum, xor_1_out, Cin);
  or or_1 (Cout, and_1_out, and_2_out);
endmodule

module _16_Bit_Adder (
  input  [15:0] A,
  input  [15:0] B,
  input  Cin,
  output [15:0] Sum,
  output V,
  output Cout
);

  wire fulladder_1_cout, fulladder_2_cout, fulladder_3_cout, fulladder_4_cout, fulladder_5_cout,
       fulladder_6_cout, fulladder_7_cout, fulladder_8_cout, fulladder_9_cout, fulladder_10_cout,
       fulladder_11_cout, fulladder_12_cout, fulladder_13_cout, fulladder_14_cout, fulladder_15_cout;

  FullAdder fulladder_1 (.A(A[0]), .B(B[0]), .Cin(Cin), .Sum(Sum[0]), .Cout(fulladder_1_cout));
  FullAdder fulladder_2 (.A(A[1]), .B(B[1]), .Cin(fulladder_1_cout), .Sum(Sum[1]), .Cout(fulladder_2_cout));
  FullAdder fulladder_3 (.A(A[2]), .B(B[2]), .Cin(fulladder_2_cout), .Sum(Sum[2]), .Cout(fulladder_3_cout));
  FullAdder fulladder_4 (.A(A[3]), .B(B[3]), .Cin(fulladder_3_cout), .Sum(Sum[3]), .Cout(fulladder_4_cout));
  FullAdder fulladder_5 (.A(A[4]), .B(B[4]), .Cin(fulladder_4_cout), .Sum(Sum[4]), .Cout(fulladder_5_cout));
  FullAdder fulladder_6 (.A(A[5]), .B(B[5]), .Cin(fulladder_5_cout), .Sum(Sum[5]), .Cout(fulladder_6_cout));
  FullAdder fulladder_7 (.A(A[6]), .B(B[6]), .Cin(fulladder_6_cout), .Sum(Sum[6]), .Cout(fulladder_7_cout));
  FullAdder fulladder_8 (.A(A[7]), .B(B[7]), .Cin(fulladder_7_cout), .Sum(Sum[7]), .Cout(fulladder_8_cout));
  FullAdder fulladder_9 (.A(A[8]), .B(B[8]), .Cin(fulladder_8_cout), .Sum(Sum[8]), .Cout(fulladder_9_cout));
  FullAdder fulladder_10 (.A(A[9]), .B(B[9]), .Cin(fulladder_9_cout), .Sum(Sum[9]), .Cout(fulladder_10_cout));
  FullAdder fulladder_11 (.A(A[10]), .B(B[10]), .Cin(fulladder_10_cout), .Sum(Sum[10]), .Cout(fulladder_11_cout));
  FullAdder fulladder_12 (.A(A[11]), .B(B[11]), .Cin(fulladder_11_cout), .Sum(Sum[11]), .Cout(fulladder_12_cout));
  FullAdder fulladder_13 (.A(A[12]), .B(B[12]), .Cin(fulladder_12_cout), .Sum(Sum[12]), .Cout(fulladder_13_cout));
  FullAdder fulladder_14 (.A(A[13]), .B(B[13]), .Cin(fulladder_13_cout), .Sum(Sum[13]), .Cout(fulladder_14_cout));
  FullAdder fulladder_15 (.A(A[14]), .B(B[14]), .Cin(fulladder_14_cout), .Sum(Sum[14]), .Cout(fulladder_15_cout));
  FullAdder fulladder_16 (.A(A[15]), .B(B[15]), .Cin(fulladder_15_cout), .Sum(Sum[15]), .Cout(Cout));
  xor xor_1 (V, fulladder_15_cout, Cout);
endmodule
