// Logisim project CPU.circ as structural Verilog: 6 circuits, main circuit CPU
module CPU (
);

  wire clock, ExtOp, MemRead, MemWrite, RegWrite;
  wire [1:0] ALUSrc, ALUSrc_t, f, PCADD, RegData, WBData;
  wire [2:0] Imm2_3, Imm5, multiplexer_3_out;
  wire [3:0] ALUOp, ALUOp_t;
  wire [4:0] Imm5_t, Op;
  wire [5:3] Imm11;
  wire [10:0] Imm11_t;
  wire [15:0] BControl, immediate_extender_1_extdimm2_3, immediate_extender_1_extdimm5,
       immediate_extender_1_extdimm11, multiplexer_1_out, multiplexer_2_out, multiplexer_4_out,
       multiplexer_5_out, n16_bit_adder_1_sum, n16_bit_adder_2_sum, PC, ram_1_data, registerfile_1_busa,
       registerfile_1_busb;

  Clock Excute (.out(clock));
  _16_Bit_Adder u_16_bit_adder_1 (
    .A(multiplexer_2_out), .B(multiplexer_1_out), .Cin(1'b0), .Sum(n16_bit_adder_1_sum));  // open: V, Cout
  Register #(.width(16)) u_PC (.D(n16_bit_adder_1_sum), .en(1'b1), .Q(PC), .clk(clock));  // open: clr
  PCCU pccu_1 (.OpCode(Op), .BControl(BControl), .PCADD(PCADD));
  Multiplexer #(.select(2), .width(16), .enable("false")) multiplexer_1 (
    .in0(16'h1), .in1(immediate_extender_1_extdimm11), .in2(immediate_extender_1_extdimm2_3),
    .in3(immediate_extender_1_extdimm5), .out(multiplexer_1_out), .sel(PCADD));
  Multiplexer #(.select(2), .width(16), .enable("false")) multiplexer_2 (
    .in0(PC), .in1(PC), .in2(PC), .in3(registerfile_1_busa), .out(multiplexer_2_out), .sel(PCADD));
  ROM #(.addrWidth(16), .dataWidth(16)) rom_1 (.addr(PC), .data({f, Imm5, Imm11, Imm2_3, Op}));  // open: sel
  Multiplexer #(.select(2), .width(3), .enable("false")) multiplexer_3 (
    .in0(Imm2_3), .in1(3'b001), .in2(3'b111), .out(multiplexer_3_out), .sel(RegData));  // open: in3
  CU cu_1 (
    .OpCode(Op), .f(f), .RegData(RegData), .ExtOp(ExtOp), .ALUSrc(ALUSrc_t), .MemWrite(MemWrite),
    .MemRead(MemRead), .WBData(WBData), .ALUOp(ALUOp_t), .RegWrite(RegWrite));
  RegisterFile registerfile_1 (
    .Rs1(Imm11), .Rs2(Imm5), .rd(multiplexer_3_out), .RegWrite(RegWrite), .BusW(multiplexer_5_out),
    .BusA(registerfile_1_busa), .BusB(registerfile_1_busb), .Clock(clock));
  Immediate_Extender immediate_extender_1 (
    .Imm5(Imm5_t), .Imm2_3({f, Imm2_3}), .ExtdImm11(immediate_extender_1_extdimm11),
    .ExtdImm5(immediate_extender_1_extdimm5), .ExtdImm2_3(immediate_extender_1_extdimm2_3), .Imm11(Imm11_t),
    .in_4(ExtOp));
  Multiplexer #(.select(2), .width(16), .enable("false")) multiplexer_4 (
    .in0(registerfile_1_busb), .in1(immediate_extender_1_extdimm11), .in2(immediate_extender_1_extdimm5),
    .in3(immediate_extender_1_extdimm2_3), .out(multiplexer_4_out), .sel(ALUSrc));
  Multiplexer #(.select(2), .width(16), .enable("false")) multiplexer_5 (
    .in0(BControl), .in1(ram_1_data), .in2(n16_bit_adder_2_sum), .in3({16{1'b0}}), .out(multiplexer_5_out),
    .sel(WBData));
  ALU alu_1 (.A(registerfile_1_busa), .B(multiplexer_4_out), .Result(BControl), .Sel(ALUOp));
  RAM #(.addrWidth(16), .dataWidth(16), .bus("separate")) ram_1 (
    .addr(BControl), .din(registerfile_1_busb), .data(ram_1_data), .str(MemWrite), .clk(clock), .ld(MemRead));  // open: sel, clr
  _16_Bit_Adder u_16_bit_adder_2 (.A(PC), .B({16{1'b0}}), .Cin(1'b1), .Sum(n16_bit_adder_2_sum));  // open: V, Cout

  // Other names for the same wires on the sheet: Rs1[2:0] = Imm11; Imm11 (some bits) = {f, Imm5, Imm2_3};
  //   Rs2[2:0] = Imm5; Rd[2:0] = Imm2_3; Imm2_3[4:3] = f; Imm5[4:3] = f

  // Notes on the sheet:
  //   contents of rom_1 (hex, n*v repeats v):
  //   34 94a f4 3967 823 8a3 11f1 bc8 b6a 923 f58f c83 ff55
endmodule

module CU (
  input  [4:0] OpCode,
  input  [1:0] f,
  output [1:0] WBData,
  output MemRead,
  output MemWrite,
  output [1:0] ALUSrc,
  output ExtOp,
  output RegWrite,
  output [1:0] RegData,
  output [3:0] ALUOp
);

  ROM #(.addrWidth(5), .dataWidth(10)) rom_1 (
    .addr(OpCode), .data({WBData, MemRead, MemWrite, ALUSrc, ExtOp, RegWrite, RegData}));  // open: sel
  ROM #(.addrWidth(7), .dataWidth(4)) rom_2 (.addr({OpCode, f}), .data(ALUOp));  // open: sel

  // Notes on the sheet:
  //   contents of rom_1 (hex, n*v repeats v):
  //   4 4 4 2c e4 e4 6*24 1ac 78 6*0 15 0 216 2ec
  //   contents of rom_2 (hex, n*v repeats v):
  //   4 5 6 0 7 8 9 0 0 1 2 3 4*0 4*2 4*3 4*4 4*5 4*6 4*7 4*8 4*9 8*0 8*1 8*2 8*3 4*a
endmodule

module Immediate_Extender (
  input  [10:0] Imm11,
  input  [4:0] Imm5,
  input  [4:0] Imm2_3,
  input  in_4,
  output [15:0] ExtdImm11,
  output [15:0] ExtdImm5,
  output [15:0] ExtdImm2_3
);

  wire [15:0] bit_extender_1_out, bit_extender_2_out;

  assign bit_extender_1_out = {{11{1'b0}}, Imm5};  // Bit_Extender bit_extender_1
  assign bit_extender_2_out = {{11{Imm5[4]}}, Imm5};  // Bit_Extender bit_extender_2
  Multiplexer #(.width(16), .enable("false")) multiplexer_1 (
    .in0(bit_extender_1_out), .in1(bit_extender_2_out), .out(ExtdImm5), .sel(in_4));
  assign ExtdImm11 = {{5{Imm11[10]}}, Imm11};  // Bit_Extender bit_extender_3
  assign ExtdImm2_3 = {{11{Imm2_3[4]}}, Imm2_3};  // Bit_Extender bit_extender_4
endmodule

module PCCU (
  input  [15:0] BControl,
  input  [4:0] OpCode,
  output [1:0] PCADD
);

  wire and_1_out, branchcontrol_1_enbranch;
  wire [1:0] rom_1_data;
  wire [1:1] or_1_out;

  BranchControl branchcontrol_1 (.BControl(BControl), .OpCode(OpCode), .ENBranch(branchcontrol_1_enbranch));
  ROM #(.addrWidth(5), .dataWidth(2)) rom_1 (.addr(OpCode), .data(rom_1_data));  // open: sel
  and and_1 (and_1_out, rom_1_data[0], rom_1_data[1]);
  or or_1 (or_1_out[1], branchcontrol_1_enbranch, and_1_out);
  assign PCADD = {or_1_out[1], 1'b1} & rom_1_data;  // AND_Gate and_2, 2 bits wide

  // Notes on the sheet:
  //   contents of rom_1 (hex, n*v repeats v):
  //   14*0 6*2 0 1 1 3
endmodule

module BranchControl (
  input  [4:0] OpCode,
  input  [15:0] BControl,
  output ENBranch
);

  wire and_1_out, and_2_out, and_3_out, and_4_out, nor_1_out, not_1_out, not_2_out, opmatch_1_en,
       opmatch_2_en, opmatch_3_en, opmatch_4_en, or_1_out, or_2_out, or_3_out, or_4_out;
  wire [4:0] multiplexer_1_out, multiplexer_2_out;
  wire [15:0] xor_1_out;

  assign xor_1_out = {16{1'b0}} ^ BControl;  // XOR_Gate xor_1, 16 bits wide
  or or_1 (or_1_out, xor_1_out[0], xor_1_out[1], xor_1_out[2], xor_1_out[3]);
  or or_2 (or_2_out, xor_1_out[4], xor_1_out[5], xor_1_out[6], xor_1_out[7]);
  or or_3 (or_3_out, xor_1_out[8], xor_1_out[9], xor_1_out[10], xor_1_out[11]);
  or or_4 (or_4_out, xor_1_out[12], xor_1_out[13], xor_1_out[14], xor_1_out[15]);
  nor nor_1 (nor_1_out, or_1_out, or_2_out, or_3_out, or_4_out);
  OpMatch opmatch_1 (.OpCode(OpCode), .ConstCode(5'b01110), .EN(opmatch_1_en));
  not not_1 (not_1_out, nor_1_out);
  Multiplexer #(.width(5), .enable("false")) multiplexer_1 (
    .in0(5'b10000), .in1(5'b10010), .out(multiplexer_1_out), .sel(OpCode[1]));
  Multiplexer #(.width(5), .enable("false")) multiplexer_2 (
    .in0(5'b10001), .in1(5'b10011), .out(multiplexer_2_out), .sel(OpCode[1]));
  not not_2 (not_2_out, BControl[0]);
  and and_1 (and_1_out, opmatch_1_en, nor_1_out);
  OpMatch opmatch_2 (.OpCode(OpCode), .ConstCode(5'b01111), .EN(opmatch_2_en));
  and and_2 (and_2_out, opmatch_2_en, not_1_out);
  and and_3 (and_3_out, opmatch_3_en, BControl[0]);
  OpMatch opmatch_3 (.OpCode(OpCode), .ConstCode(multiplexer_1_out), .EN(opmatch_3_en));
  OpMatch opmatch_4 (.OpCode(OpCode), .ConstCode(multiplexer_2_out), .EN(opmatch_4_en));
  and and_4 (and_4_out, opmatch_4_en, not_2_out);
  or or_5 (ENBranch, and_1_out, and_2_out, and_3_out, and_4_out);

  // Other names for the same wires on the sheet: Op[4:0] = OpCode

  // Notes on the sheet:
  //   BEQ
  //   BNE
  //   BLT || BLTU
  //   BGE || BGEU
endmodule

module OpMatch (
  input  [4:0] OpCode,
  input  [4:0] ConstCode,
  output EN
);

  wire [4:0] xnor_1_out;

  assign xnor_1_out = ~(OpCode ^ ConstCode);  // XNOR_Gate xnor_1, 5 bits wide
  and and_1 (EN, xnor_1_out[0], xnor_1_out[1], xnor_1_out[2], xnor_1_out[3], xnor_1_out[4]);
endmodule
